// Digital circuit dtack_circuit.dig as structural Verilog
module dtack_circuit (
  input  nROMDTACK,
  input  nRAMDTACK,
  input  nDUARTDTACK,
  input  nBUSDTACK,
  output nDTACK
);

  wire nand_1_out;

  nand nand_1 (nand_1_out, nROMDTACK, nRAMDTACK, nDUARTDTACK, nBUSDTACK);
  not not_1 (nDTACK, nand_1_out);
endmodule
