// Digital circuit irq_glue_logic.dig as structural Verilog
module irq_glue_logic (
  input  A0,
  input  A1,
  input  A2,
  input  AS,
  input  FC0,
  input  FC1,
  input  FC2,
  output out_8,
  output out_9,
  output out_10,
  output out_11,
  output out_12,
  output out_13,
  output out_14,
  output out_15
);

  wire _74138_1_pin5;

  _74138 _74138_1 (
    .pin1(A0), .pin2(A1), .pin3(A2), .pin4(AS), .pin5(_74138_1_pin5), .pin6(1'b1), .pin7(out_14),
    .pin8(1'b0), .pin9(out_15), .pin10(out_8), .pin11(out_10), .pin12(out_9), .pin13(out_13), .pin14(out_12),
    .pin15(out_11), .pin16(1'b1));
  _74138 _74138_2 (
    .pin1(FC0), .pin2(FC1), .pin3(FC2), .pin4(AS), .pin5(1'b0), .pin6(1'b1), .pin7(_74138_1_pin5),
    .pin8(1'b0), .pin16(1'b1));  // open: pin9, pin10, pin11, pin12, pin13, pin14, pin15
endmodule
